# Fritzing sketch _002_doors_v_1_client (saved by Fritzing 0.7.12b)

parts:
  U1 = Arduino Mega
  J1 = Generic female header - 4 pins [package=THT]
  J2 = Generic female header - 4 pins [package=THT]
  J3 = Generic female header - 4 pins [package=THT]
  S1 = Pushbutton [package="[THT]"]

nets:
  GND: U1.GND, J1.pin1, J3.pin3, J3.pin4, S1.Pin_3, S1.Pin_4
  N1: U1.D10, J2.pin2
  N2: U1.D9, J1.pin2
  N3: U1.D3, J3.pin1
  N4: U1.D2, J3.pin2
  N5: U1.RST, S1.Pin_1, S1.Pin_2
  N6: U1.3V3, J2.pin1
  N7: U1.D50, J1.pin4
  N8: U1.D51, J2.pin3
  N9: U1.D52, J1.pin3
