# Fritzing sketch focuser_C5_rec (saved by Fritzing 0.9.1b)
circuit board: 11.4214cm x 7.55794cm
breadboards: 1

parts:
  J2 = male pin header, 4 pins [form="♂ (male)"]
  motor_PWR = Power Jack [package=power_jack_pth_lock]
  S2 = Momentary Switch [package=ksa_sealed_tac_switch]
  J4 = female pin header, 2 pins [form="♀ (female)"]
  J5 = female pin header, 2 pins [form="♀ (female)"]
  X1 = DB9 Connector [package=db9]
  J1 = male pin header, 3 pins [form="♂ (male)"]
  S1 = Momentary Switch [package=ksa_sealed_tac_switch]
  C5 = Arduino Nano v2.3

nets:
  N1: J2.pin1, C5.D8
  N2: J2.pin2, C5.D9
  N3: J2.pin3, C5.D10
  N4: J2.pin4, C5.D11
  N5: motor_PWR.PWR, J1.pin1
  N6: S2.1, C5.D5
  N7: J4.pin1, X1.7
  N8: J4.pin2, X1.6
  N9: J5.pin1, X1.8
  N10: J5.pin2, X1.9
  N11: X1.3, C5.D3
  N12: X1.4, C5.D2
  N13: S1.1, C5.D4

notes:
  12V
  GND
