# Fritzing sketch focuser_C5_smaller (saved by Fritzing 0.9.1b)
circuit board: 9.67163cm x 7.79783cm
breadboards: 1

parts:
  J2 = male pin header, 4 pins [form="♂ (male)"]
  S2 = Momentary Switch [package=ksa_sealed_tac_switch]
  J1 = male pin header, 3 pins [form="♂ (male)"]
  S1 = Momentary Switch [package=ksa_sealed_tac_switch]
  J4 = male pin header, 2 pins [form="♂ (male)"]
  J5 = male pin header, 2 pins [form="♂ (male)"]
  X1 = DB9 Connector [package=db9]
  C5 = Arduino Nano v2.3
  motor_PWR = Power Jack [package=power_jack_pth_lock]

nets:
  N1: J2.pin1, C5.D11
  N2: J2.pin2, C5.D10
  N3: J2.pin3, C5.D9
  N4: J2.pin4, C5.D8
  N5: S2.1, C5.D5
  GND: S2.4, J1.pin2, S1.4, X1.1, X1.5, C5.GND, motor_PWR.GND, motor_PWR.GNDBREAK
  N6: J1.pin1, motor_PWR.PWR
  N7: S1.1, C5.D4
  N8: J4.pin1, X1.7
  N9: J4.pin2, X1.6
  N10: J5.pin1, X1.8
  N11: J5.pin2, X1.9
  N12: X1.3, C5.D2
  N13: X1.4, C5.D3

notes:
  12V
  GND
  +F
  -F
  USB
